# Fritzing sketch circuit (saved by Fritzing 0.9.3b)
breadboards: 1

parts:
  Part1 = Arduino Uno (Rev3)
  R1 = Trimmer Potentiometer [maximum_resistance=10kΩ package=THT]
  R2 = Trimmer Potentiometer [maximum_resistance=10kΩ package=THT]
  J1 = Basic Servo
  J2 = Basic Servo

nets:
  N1: Part1.A0, R1.wiper
  N2: Part1.A1, R2.wiper
  N3: Part1.D10_PWM/SS, J2.pulse
  N4: Part1.D11_PWM/MOSI, J1.pulse
  GND: Part1.GND, R1.leg2, R2.leg2, J1.gnd, J2.gnd
  VCC: Part1.5V, R1.leg1, R2.leg1, J1.vcc, J2.vcc

notes:
  Rotation
  Normal
